# Fritzing sketch collegamenti (saved by Fritzing 0.9.3b)
breadboards: 1

parts:
  Componente1 = Arduino Nano RP2040
  S2 = Pushbutton [package="[THT]"]
  LED1 = LED - 5mm [color="Green (555nm)" package="5 mm [THT]"]
  LED2 = LED - 5mm [color="Blue (430nm)" package="5 mm [THT]"]
  LED3 = LED - 5mm [color="Red (633nm)" package="5 mm [THT]"]
  LED4 = LED - 5mm [color="White (6500K)" package="5 mm [THT]"]
  LED5 = LED - 5mm [color="Yellow (595nm)" package="5 mm [THT]"]
  R1 = Resistor [tolerance=±5% resistance=220 package=THT]
  R2 = Resistor [tolerance=±5% resistance=220 package=THT]
  R3 = Resistor [tolerance=±5% resistance=220 package=THT]
  R4 = Resistor [tolerance=±5% resistance=220 package=THT]
  R5 = Resistor [tolerance=±5% resistance=220 package=THT]
  S1 = Pushbutton [package="[THT]"]

nets:
  N1: Componente1.RESET, Componente1.A7
  N2: Componente1.GND, Componente1.D13~, S2.Pin_3, S2.Pin_4, LED1.cathode, LED2.cathode, LED3.cathode, LED4.cathode, LED5.cathode, S1.Pin_3, S1.Pin_4
  N3: Componente1.D2, R1.Pin_0
  N4: Componente1.D3~, R2.Pin_0
  N5: Componente1.D4, R3.Pin_0
  N6: Componente1.D5~, R4.Pin_0
  N7: Componente1.D6~, R5.Pin_0
  N8: Componente1.D11/MOSI, Componente1.+5V, S2.Pin_1, S2.Pin_2
  N9: Componente1.D12~/MISO, S1.Pin_1, S1.Pin_2
  N10: LED1.anode, R1.Pin_1
  N11: LED2.anode, R2.Pin_1
  N12: LED3.anode, R3.Pin_1
  N13: LED4.anode, R4.Pin_1
  N14: LED5.anode, R5.Pin_1

notes:
  BUTTON_1 -> pin 12
  BUTTON_2 -> pin 11
  LEDGREEN -> pin 2
  LEDBLUE -> pin 3
  LEDRED -> pin 4
  LEDWHITE -> pin 5
  LEDYELLOW -> pin 6
  x5 RESISTOR 220Ω
  x2 BUTTON

custom parts:
  Arduino Nano RP2040: At the core of the Arduino Nano RP2040 Connect is the Raspberry Pi RP2040; a dual-core Arm Cortex M0+ processor, with the on-board ESP32 being available as a co-processor. There’s 16MB of flash memory that’s off-chip, providing plenty of room for code and storage. The highly adaptable u-blox NINA-W102 WiFi and Bluetooth radio module provides connectivity, allowing the device to harness the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
